# Fritzing sketch Sketch (saved by Fritzing 0.9.9b)
breadboards: 1

parts:
  J1 = Basic Servo
  J2 = Basic Servo
  J3 = Basic Servo
  U1 = ESP32S-HiLetgo [part_number=ESP32S-HiLetgo]
  BAT1 = BC9VPC [package=bc9vpc]
  M1 = RioRand LM2596
  부품1 = Motor Driver 1A Dual TB6612FNG
  M2 = DC Motor
  M3 = DC Motor
  DFRobot_DFPlayer_Mini1 = DFRobot DFPlayer Mini [part_number=DFR0299]
  SP1 = SPEAKER [package=pcb_mount_speaker]
  LED1 = smd LED [color="Blue (505nm)" package="1206 [SMD]"]
  LED2 = smd LED [color="Red (633nm)" package="1206 [SMD]"]
  LED3 = smd LED [color="Red (633nm)" package="1206 [SMD]"]
  LED4 = smd LED [color="Red (633nm)" package="1206 [SMD]"]

nets:
  GND: J1.gnd, J2.gnd, J3.gnd, U1.GND, M1.Pin_4, DFRobot_DFPlayer_Mini1.GND-1, LED1.cathode, LED2.cathode, LED3.cathode, LED4.cathode
  VCC: J1.vcc, J2.vcc, J3.vcc, U1.VIN, M1.Pin_3, DFRobot_DFPlayer_Mini1.VCC
  N1: J1.pulse, U1.GPIO25
  N2: J2.pulse, U1.GPIO22
  N3: J3.pulse, U1.GPIO27
  N4: U1.GPIO32, LED4.anode
  N5: U1.GPIO33, 부품1.BIN1
  N6: U1.GPIO26, 부품1.AIN1
  N7: U1.GPIO2, LED1.anode
  N8: U1.GPIO4, LED2.anode
  N9: U1.GPIO16, DFRobot_DFPlayer_Mini1.TX
  N10: U1.GPIO17, DFRobot_DFPlayer_Mini1.RX
  N11: U1.GPIO18, 부품1.AIN2
  N12: U1.GPIO19, 부품1.BIN2
  N13: U1.GPIO21, LED3.anode
  N14: BAT1.V+, M1.Pin_1, 부품1.VCC
  N15: BAT1.V-, M1.Pin_2, 부품1.GND
  N16: 부품1.B01, M3.pin_1
  N17: 부품1.B02, M3.pin_2
  N18: 부품1.A02, M2.pin_1
  N19: 부품1.A01, M2.pin_2
  N20: DFRobot_DFPlayer_Mini1.SPK_1, SP1.+
  N21: DFRobot_DFPlayer_Mini1.SPK_2, SP1.-

notes:
  Waist
  Arm1
  Arm2
  Track1
  Track2
  Cannon
  Gattling1
  Gattling2

custom parts:
  ESP32S-HiLetgo: HiLetgo ESP-WROOM-32 ESP32 ESP-32S Development Board 2.4GHz Dual-Mode WiFi + Bluetooth Dual Cores Microcontroller The ESP32 integrated with Antenna switches, RF Balun, power amplifiers, low-noise amplifiers, filters, and management modules, and the entire solution occupies the least area of PCB. 2.4 GHz Wi-Fi plus Bluetooth dual-mode chip, with TSMC Ultra-low power consumption 40nm technology,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
